# Fritzing sketch WeatherStation (saved by Fritzing 0.9.2b)
breadboards: 1

parts:
  Part1 = Arduino Uno (Rev3)
  RHT1 = Humidity and Temperature Sensor RHT03
  R1 = Resistor [tolerance=±5% resistance=10k package=THT]
  R2 = PHOTOCELL [package=photocell]
  R3 = Resistor [tolerance=±5% resistance=10k package=THT]
  Part2 = Humidity Temperature Sensor SHT15

nets:
  N1: Part1.A0, R2.P$2, R3.Pin_0
  N2: Part1.A4/SDA, Part2.SCL
  N3: Part1.A5/SCL, Part2.SDA
  VCC: RHT1.Vcc, RHT1.Data-signal, R1.Pin_0, R1.Pin_1, R2.P$1, Part2.VCC
  N4: RHT1.GND_2, R3.Pin_1, Part2.GND
